# Fritzing sketch example_keypad_3x3 (saved by Fritzing 0.9.10b)
breadboards: 1

parts:
  S1 = Cherry MX Keyswitch
  S2 = Cherry MX Keyswitch
  S3 = Cherry MX Keyswitch
  S4 = Cherry MX Keyswitch
  S5 = Cherry MX Keyswitch
  S6 = Cherry MX Keyswitch
  S7 = Cherry MX Keyswitch
  S8 = Cherry MX Keyswitch
  S9 = Cherry MX Keyswitch
  D1 = Diode [package=diode-1n4148]
  D2 = Diode [package=diode-1n4148]
  D3 = Diode [package=diode-1n4148]
  D4 = Diode [package=diode-1n4148]
  D5 = Diode [package=diode-1n4148]
  D6 = Diode [package=diode-1n4148]
  D7 = Diode [package=diode-1n4148]
  D8 = Diode [package=diode-1n4148]
  D9 = Diode [package=diode-1n4148]

nets:
  N1: S1.pin_3, D1.A
  pin r0: S1.pin_9, S1.pin_10, S2.pin_1, S2.pin_9, S2.pin_10, S3.pin_1, S3.pin_10
  N2: S2.pin_3, D4.A
  N3: S3.pin_3, D9.A
  N4: S4.pin_3, D2.A
  pin r1: S4.pin_9, S4.pin_10, S5.pin_1, S5.pin_9, S5.pin_10, S6.pin_1, S6.pin_10
  N5: S5.pin_3, D5.A
  N6: S6.pin_3, D8.A
  N7: S7.pin_3, D3.A
  pin r2: S7.pin_9, S7.pin_10, S8.pin_1, S8.pin_9, S8.pin_10, S9.pin_1, S9.pin_10
  N8: S8.pin_3, D6.A
  N9: S9.pin_3, D7.A
  pin c0: D1.C, D2.C, D3.C
  pin c1: D4.C, D5.C, D6.C
  pin c2: D7.C, D8.C, D9.C
